// Logisim project TP03.circ as structural Verilog: 5 circuits, main circuit main
module main (
  input  a3,
  input  a2,
  input  a1,
  input  a0,
  input  b3,
  input  b2,
  input  b1,
  input  b0,
  input  minus_b,
  input  p1,
  input  p0,
  output s0,
  output s1,
  output s2,
  output s3,
  output carry_out
);

  ULA4b ula4b_1 (
    .s0(s0), .s1(s1), .s2(s2), .s3(s3), .a0(a0), .a1(a1), .a2(a2), .a3(a3), .b0(b0), .b1(b1), .b2(b2),
    .b3(b3), .b_invertido(minus_b), .carry_out(carry_out), .op1(p1), .op0(p0));
endmodule

module ULA4b (
  input  op1,
  input  op0,
  input  a3,
  input  a2,
  input  a1,
  input  a0,
  input  b3,
  input  b2,
  input  b1,
  input  b0,
  input  b_invertido,
  output s0,
  output s1,
  output s2,
  output s3,
  output carry_out
);

  wire ula_1_carry_out, ula_2_carry_out, ula_3_carry_out;

  ULA ula_1 (
    .a(a0), .b(b0), .S(s0), .b_invertido(b_invertido), .carry_in(b_invertido), .carry_out(ula_1_carry_out),
    .Op1(op1), .Op0(op0));
  ULA ula_2 (
    .a(a1), .b(b1), .S(s1), .b_invertido(b_invertido), .carry_in(ula_1_carry_out),
    .carry_out(ula_2_carry_out), .Op1(op1), .Op0(op0));
  ULA ula_3 (
    .a(a2), .b(b2), .S(s2), .b_invertido(b_invertido), .carry_in(ula_2_carry_out),
    .carry_out(ula_3_carry_out), .Op1(op1), .Op0(op0));
  ULA ula_4 (
    .a(a3), .b(b3), .S(s3), .b_invertido(b_invertido), .carry_in(ula_3_carry_out), .carry_out(carry_out),
    .Op1(op1), .Op0(op0));
endmodule

module ULA (
  input  b_invertido,
  input  carry_in,
  input  Op1,
  input  Op0,
  input  a,
  input  b,
  output S,
  output carry_out
);

  wire and_1_out, and_2_out, and_3_out, and_4_out, and_5_out, multiplexer_1_out, not_1_out, not_2_out,
       not_3_out, not_4_out, not_5_out, not_6_out, or_1_out, somador_completo_1_s;

  Multiplexer #(.enable("false")) multiplexer_1 (.in0(b), .in1(not_1_out), .out(multiplexer_1_out), .sel(b_invertido));
  not not_1 (not_1_out, b);
  and and_1 (and_1_out, a, multiplexer_1_out);
  or or_1 (or_1_out, a, multiplexer_1_out);
  not not_2 (not_2_out, a);
  somador_completo somador_completo_1 (
    .a(a), .b(multiplexer_1_out), .S(somador_completo_1_s), .carry_in(carry_in), .carry_out(carry_out));
  not not_3 (not_3_out, Op1);
  not not_4 (not_4_out, Op0);
  not not_5 (not_5_out, Op1);
  not not_6 (not_6_out, Op0);
  and and_2 (and_2_out, not_3_out, not_4_out, and_1_out);
  and and_3 (and_3_out, not_5_out, Op0, or_1_out);
  and and_4 (and_4_out, Op1, not_6_out, not_2_out);
  and and_5 (and_5_out, Op0, Op1, somador_completo_1_s);
  or or_2 (S, and_2_out, and_3_out, and_4_out, and_5_out);
endmodule

module somador_completo (
  input  carry_in,
  input  a,
  input  b,
  output S,
  output carry_out
);

  wire somador_simples_1_carry_out, somador_simples_1_s, somador_simples_2_carry_out;

  somador_simples somador_simples_1 (.a(a), .b(b), .s(somador_simples_1_s), .carry_out(somador_simples_1_carry_out));
  or or_1 (carry_out, somador_simples_1_carry_out, somador_simples_2_carry_out);
  somador_simples somador_simples_2 (
    .a(carry_in), .b(somador_simples_1_s), .s(S), .carry_out(somador_simples_2_carry_out));
endmodule

module somador_simples (
  input  a,
  input  b,
  output s,
  output carry_out
);

  and and_1 (carry_out, a, b);
  xor xor_1 (s, a, b);
endmodule
