// Logisim project ULA.circ as structural Verilog: 2 circuits, main circuit main
module main (
  input  [3:0] in_1,
  input  [3:0] in_2,
  input  in_3,
  input  in_4,
  input  [1:0] in_5,
  output [3:0] out_6,
  output carry_in
);

  wire ula_1_carry_out, ula_2_carry_out, ula_3_carry_out;

  ULA ula_1 (
    .a(in_2[0]), .b(in_1[0]), .Resp(out_6[0]), .carry_in(in_4), .invert_b(in_3), .carry_out(ula_1_carry_out),
    .Oper(in_5));
  ULA ula_2 (
    .a(in_2[1]), .b(in_1[1]), .Resp(out_6[1]), .carry_in(ula_1_carry_out), .invert_b(in_3),
    .carry_out(ula_2_carry_out), .Oper(in_5));
  ULA ula_3 (
    .a(in_2[2]), .b(in_1[2]), .Resp(out_6[2]), .carry_in(ula_2_carry_out), .invert_b(in_3),
    .carry_out(ula_3_carry_out), .Oper(in_5));
  ULA ula_4 (
    .a(in_2[3]), .b(in_1[3]), .Resp(out_6[3]), .carry_in(ula_3_carry_out), .invert_b(in_3),
    .carry_out(carry_in), .Oper(in_5));
endmodule

module ULA (
  input  carry_in,
  input  a,
  input  b,
  input  [1:0] Oper,
  input  invert_b,
  output Resp,
  output carry_out
);

  wire adder_1_out, and_1_out, multiplexer_1_out, not_1_out, or_1_out;

  Multiplexer #(.enable("false")) multiplexer_1 (.in0(b), .in1(not_1_out), .out(multiplexer_1_out), .sel(invert_b));
  not not_1 (not_1_out, b);
  and and_1 (and_1_out, a, multiplexer_1_out);
  or or_1 (or_1_out, a, multiplexer_1_out);
  Adder #(.width(1)) adder_1 (.a(a), .b(multiplexer_1_out), .out(adder_1_out), .cin(carry_in), .cout(carry_out));
  Multiplexer #(.select(2), .enable("false")) multiplexer_2 (
    .in0(and_1_out), .in1(or_1_out), .in2(adder_1_out), .out(Resp), .sel(Oper));  // open: in3
endmodule
